// Logisim project ALU.circut.circ as structural Verilog: 3 circuits, main circuit AU
module AU (
  input  Cin,
  input  [3:0] A,
  input  [3:0] B,
  output [3:0] Y,
  output Overflow,
  output Cout
);

  wire adder_1_cout, adder_2_cout, adder_3_cout;

  Adder #(.width(1)) adder_1 (.a(A[0]), .b(B[0]), .out(Y[0]), .cin(Cin), .cout(adder_1_cout));
  Adder #(.width(1)) adder_2 (.a(A[1]), .b(B[1]), .out(Y[1]), .cin(adder_1_cout), .cout(adder_2_cout));
  Adder #(.width(1)) adder_3 (.a(A[2]), .b(B[2]), .out(Y[2]), .cin(adder_2_cout), .cout(adder_3_cout));
  Adder #(.width(1)) adder_4 (.a(A[3]), .b(B[3]), .out(Y[3]), .cin(adder_3_cout), .cout(Cout));
  xor xor_1 (Overflow, adder_3_cout, Cout);
endmodule

module LU (
  input  [3:0] A,
  input  [3:0] B,
  input  f2,
  input  f0,
  output [3:0] Y
);

  wire [3:0] and_1_out, or_1_out, xor_1_out;

  assign and_1_out = A & B;  // AND_Gate and_1, 4 bits wide
  assign or_1_out = A | B;  // OR_Gate or_1, 4 bits wide
  assign xor_1_out = A ^ B;  // XOR_Gate xor_1, 4 bits wide
  Multiplexer #(.enable("true"), .select(2), .width(4)) multiplexer_1 (
    .in0(and_1_out), .in1(or_1_out), .in2(xor_1_out), .in3(B), .out(Y), .sel({f2, f0}));  // open: en
endmodule

module ALU (
  input  [3:0] A,
  input  [3:0] B,
  input  [3:0] OP,
  output V,
  output C,
  output Z,
  output out_7,
  output [3:0] Y
);

  wire [3:0] au_1_y, lu_1_y, multiplexer_1_out, multiplexer_2_out, not_1_out, not_2_out;

  assign not_1_out = ~A;  // NOT_Gate not_1, 4 bits wide
  assign not_2_out = ~B;  // NOT_Gate not_2, 4 bits wide
  Multiplexer #(.enable("true"), .width(4)) multiplexer_1 (
    .in0(A), .in1(not_1_out), .out(multiplexer_1_out), .sel(OP[0]));  // open: en
  Multiplexer #(.enable("true"), .width(4)) multiplexer_2 (
    .in0(B), .in1(not_2_out), .out(multiplexer_2_out), .sel(OP[1]));  // open: en
  AU au_1 (.A(multiplexer_1_out), .B(multiplexer_2_out), .Cin(OP[2]), .Cout(C), .Y(au_1_y), .Overflow(V));
  LU lu_1 (.B(multiplexer_2_out), .A(A), .f2(OP[2]), .f0(OP[0]), .Y(lu_1_y));
  Multiplexer #(.enable("true"), .width(4)) multiplexer_3 (
    .in0(au_1_y), .in1(lu_1_y), .out({out_7, Y[2:0]}), .sel(OP[3]));  // open: en
  nor nor_1 (Z, Y[0], Y[1], Y[2], out_7);

  assign Y[3] = out_7;
endmodule
