// Logisim project PC_8bit.circ as structural Verilog: 3 circuits, main circuit PC_8bit_main
module PC_8bit_main (
  input  RESET,
  output [3:0] INSTRUCTION_OUT
);

  wire clock_1_out;
  wire [7:0] programcounter8bit_1_pc_out;

  Clock clock_1 (.out(clock_1_out));
  ProgramCounter8bit programcounter8bit_1 (.RESET(RESET), .PC_OUT(programcounter8bit_1_pc_out));
  memory8bit memory8bit_1 (.ADDRESS(programcounter8bit_1_pc_out), .INSTRUCTION_OUT(INSTRUCTION_OUT));
endmodule

module ProgramCounter8bit (
  input  RESET,
  output [7:0] PC_OUT
);

  wire clock_1_out;
  wire [7:0] adder_1_out;

  Clock clock_1 (.out(clock_1_out));
  Register register_1 (.D(adder_1_out), .en(1'b1), .clk(clock_1_out), .Q(PC_OUT), .clr(RESET));
  Adder adder_1 (.a(PC_OUT), .b(8'h1), .out(adder_1_out));  // open: cin, cout
endmodule

module memory8bit (
  input  [7:0] ADDRESS,
  output [3:0] INSTRUCTION_OUT
);

  ROM #(.dataWidth(4)) rom_1 (.addr(ADDRESS), .data(INSTRUCTION_OUT));

  // Notes on the sheet:
  //   contents of rom_1 (hex, n*v repeats v):
  //   0 1 2 3 4
endmodule
