// Logisim project Jump.circ..circ as structural Verilog: 2 circuits, main circuit Jump_main
module Jump_main (
  input  [3:0] INSTRUCTION,
  input  Z_FLAG,
  output [2:0] ALU_OP,
  output REG_SELECT,
  output REG_LOAD,
  output MEM_WRITE,
  output JUMP_ENABLE
);

  wire decoder_1_out0, decoder_1_out5;

  and and_1 (JUMP_ENABLE, decoder_1_out5, Z_FLAG);
  or or_1 (REG_LOAD, decoder_1_out0, REG_SELECT);
  Decoder #(.enable("false"), .select(4)) decoder_1 (
    .out0(decoder_1_out0), .out1(REG_SELECT), .out3(ALU_OP[0]), .out4(MEM_WRITE), .out5(decoder_1_out5),
    .sel(INSTRUCTION));  // open: out2, out6, out7, out8, out9, out10, out11, out12, out13, out14, out15

  assign ALU_OP[2:1] = 2'b00;
endmodule

module Control_Unit (
  input  in_1,
  input  in_2,
  input  [3:0] INSTRUCTION,
  input  in_4,
  input  in_5
);

  Jump_main jump_main_1 ();  // open: ALU_OP, INSTRUCTION, REG_SELECT, Z_FLAG, REG_LOAD, MEM_WRITE, JUMP_ENABLE
endmodule
