// Logisim project ControlUnit.circ as structural Verilog: 2 circuits, main circuit CU_main
module CU_main (
  input  [3:0] INSTRUCTION,
  output [2:0] ALU_OP,
  output REG_SELECT,
  output REG_LOAD,
  output MEM_WRITE
);

  wire decoder_1_out0;

  or or_1 (REG_LOAD, decoder_1_out0, REG_SELECT);
  Decoder #(.enable("false"), .select(4)) decoder_1 (
    .out0(decoder_1_out0), .out1(REG_SELECT), .out3(ALU_OP[0]), .out4(MEM_WRITE), .sel(INSTRUCTION));  // open: out2, out5, out6, out7, out8, out9, out10, out11, out12, out13, out14, out15

  assign ALU_OP[2:1] = 2'b00;
endmodule

module ControlUnit (
  input  ALU_OP,
  input  REG_SELECT,
  input  [3:0] INSTRUCTION,
  input  REG_LOAD,
  input  MEM_WRITE
);

  CU_main cu_main_1 ();  // open: ALU_OP, INSTRUCTION, REG_SELECT, REG_LOAD, MEM_WRITE
endmodule
