// Logisim project PC_Memory_v3.circ as structural Verilog: 4 circuits, main circuit main
module main (
  input  RESET,
  output [3:0] INSTRUCTION_OUT
);

  wire clock_1_out;
  wire [3:0] programcounter_1_pc_out;

  Clock clock_1 (.out(clock_1_out));
  ProgramCounter programcounter_1 (.in_1(clock_1_out), .Reset(RESET), .PC_OUT(programcounter_1_pc_out));
  Memory memory_1 (.ADDRESS(programcounter_1_pc_out), .INSTRUCTION_OUT(INSTRUCTION_OUT));
endmodule

module ProgramCounter (
  input  in_1,
  input  Reset,
  output [3:0] PC_OUT
);

  wire clock_1_out;
  wire [3:0] adder_1_out;

  Clock clock_1 (.out(clock_1_out));
  Register #(.width(4)) register_1 (.D(adder_1_out), .clk(clock_1_out), .Q(PC_OUT), .clr(Reset));  // open: en
  Adder #(.width(4)) adder_1 (.a(PC_OUT), .b(4'b0001), .out(adder_1_out));  // open: cin, cout
endmodule

module Memory (
  input  [3:0] ADDRESS,
  output [3:0] INSTRUCTION_OUT
);

  ROM #(.addrWidth(4), .dataWidth(4)) memory (.addr(ADDRESS), .data(INSTRUCTION_OUT));

  // Notes on the sheet:
  //   contents of memory (hex, n*v repeats v):
  //   0 1 2 3 4
endmodule

module main_cpu (
  input  RESET
);

  wire Clock1_out, CU_reg_select;
  wire [2:0] CU_alu_op;
  wire [3:0] ALU_Circuit_p4, bit_extender_1_out, memory_1_instruction_out, programcounter_1_pc_out;

  Clock Clock1 (.out(Clock1_out));
  RegisterFile registerfile_1 (
    .Data_In(ALU_Circuit_p4), .Clock(Clock1_out), .SELECTT(CU_reg_select), .DATAIN(ALU_Circuit_p4),
    .clk(Clock1_out));  // open: Load_A, REG_A_OUT, Load_B, REG_B_OUT
  ProgramCounter programcounter_1 (.in_1(RESET), .Reset(Clock1_out), .PC_OUT(programcounter_1_pc_out));
  CU_main CU (
    .ALU_OP(CU_alu_op), .INSTRUCTION(memory_1_instruction_out), .REG_SELECT(CU_reg_select));  // open: REG_LOAD, MEM_WRITE
  assign bit_extender_1_out = {{1{1'b0}}, CU_alu_op};  // Bit_Extender bit_extender_1
  // ALU ALU_Circuit: pin names not known; wires that end beside it: 4'b0001, bit_extender_1_out, bit_extender_1_out, ALU_Circuit_p4
  Memory memory_1 (.ADDRESS(programcounter_1_pc_out), .INSTRUCTION_OUT(memory_1_instruction_out));
endmodule
