// Logisim project PC_Memory.circ as structural Verilog: 3 circuits, main circuit main
module main (
  input  RESET,
  output [3:0] INSTRUCTION_OUT
);

  wire clock_1_out;
  wire [3:0] programcounter_1_pc_out;

  Clock clock_1 (.out(clock_1_out));
  ProgramCounter programcounter_1 (.in_1(clock_1_out), .Reset(RESET), .PC_OUT(programcounter_1_pc_out));
  Memory memory_1 (.ADDRESS(programcounter_1_pc_out), .INSTRUCTION_OUT(INSTRUCTION_OUT));
endmodule

module ProgramCounter (
  input  in_1,
  input  Reset,
  output [3:0] PC_OUT
);

  wire clock_1_out;
  wire [3:0] adder_1_out;

  Clock clock_1 (.out(clock_1_out));
  Register #(.width(4)) register_1 (.D(adder_1_out), .clk(clock_1_out), .Q(PC_OUT), .clr(Reset));  // open: en
  Adder #(.width(4)) adder_1 (.a(PC_OUT), .b(4'b0001), .out(adder_1_out));  // open: cin, cout
endmodule

module Memory (
  input  [3:0] ADDRESS,
  output [3:0] INSTRUCTION_OUT
);

  ROM #(.addrWidth(4), .dataWidth(4)) memory (.addr(ADDRESS), .data(INSTRUCTION_OUT));

  // Notes on the sheet:
  //   contents of memory (hex, n*v repeats v):
  //   0 1 2 3 4
endmodule
