// Logisim project PC_Memory_backup.circ as structural Verilog: 4 circuits, main circuit main
module main (
  input  RESET,
  output [3:0] INSTRUCTION_OUT
);

  wire clock_1_out;
  wire [3:0] programcounter_1_pc_out;

  Clock clock_1 (.out(clock_1_out));
  ProgramCounter programcounter_1 (.clk_in(clock_1_out), .Reset(RESET), .PC_OUT(programcounter_1_pc_out));
  Memory memory_1 (.ADDRESS(programcounter_1_pc_out), .INSTRUCTION_OUT(INSTRUCTION_OUT));
endmodule

module ProgramCounter (
  input  clk_in,
  input  Reset,
  output [3:0] PC_OUT
);

  wire [3:0] adder_1_out;

  Register #(.width(4)) register_1 (.D(adder_1_out), .en(1'b1), .clk(clk_in), .Q(PC_OUT), .clr(Reset));
  Adder #(.width(4)) adder_1 (.a(PC_OUT), .b(4'b0001), .out(adder_1_out));  // open: cin, cout
endmodule

module Memory (
  input  [3:0] ADDRESS,
  output [3:0] INSTRUCTION_OUT
);

  ROM #(.addrWidth(4), .dataWidth(4)) memory (.addr(ADDRESS), .data(INSTRUCTION_OUT));

  // Notes on the sheet:
  //   contents of memory (hex, n*v repeats v):
  //   0 1 2 3 4
endmodule

module main_cpu (
  input  RESET,
  output MEM_WRITE_INDICATOR,
  output Z_FLAG,
  output O_FLAG,
  output C_FLAG
);

  wire Clock1_out, CU_C_jump_enable, CU_C_reg_load, CU_C_reg_select;
  wire [2:0] CU_C_alu_op;
  wire [3:0] ALU_C_y, bit_extender_1_out, memory_1_instruction_out, programcounter_1_pc_out,
       registerfile_1_reg_a_out, registerfile_1_reg_b_out;

  Clock Clock1 (.out(Clock1_out));
  ProgramCounter programcounter_1 (.clk_in(RESET), .Reset(Clock1_out), .PC_OUT(programcounter_1_pc_out));
  RegisterFile registerfile_1 (
    .Data_In(ALU_C_y), .Clock(Clock1_out), .Load_A(CU_C_reg_load), .SELECTT(CU_C_reg_select),
    .DATAIN(ALU_C_y), .clk(Clock1_out), .Load_B(CU_C_reg_load), .REG_A_OUT(registerfile_1_reg_a_out),
    .REG_B_OUT(registerfile_1_reg_b_out));
  Jump_main CU_C (
    .ALU_OP(CU_C_alu_op), .INSTRUCTION(memory_1_instruction_out), .REG_SELECT(CU_C_reg_select),
    .Z_FLAG(1'b0), .REG_LOAD(CU_C_reg_load), .MEM_WRITE(MEM_WRITE_INDICATOR), .JUMP_ENABLE(CU_C_jump_enable));
  assign bit_extender_1_out = {{1{1'b0}}, CU_C_alu_op};  // Bit_Extender bit_extender_1
  Memory memory_1 (.ADDRESS(programcounter_1_pc_out), .INSTRUCTION_OUT(memory_1_instruction_out));
  ALU ALU_C (
    .A(registerfile_1_reg_a_out), .B(registerfile_1_reg_b_out), .OP(bit_extender_1_out), .V(O_FLAG),
    .C(C_FLAG), .Z(Z_FLAG), .Y(ALU_C_y));  // open: out_7
  LED JUMP_ENABLE (.in(CU_C_jump_enable));
endmodule
