// Logisim project Registers.circ as structural Verilog
module RegisterFile (
  input  [3:0] Data_In,
  input  Clock,
  input  Load_A,
  input  [3:0] REG_A_OUT,
  input  SELECTT,
  input  [3:0] DATAIN,
  input  clk,
  input  Load_B,
  input  [3:0] REG_B_OUT
);

  wire and_3_out, and_4_out, not_1_out;

  not not_1 (not_1_out, SELECTT);
  // AND_Gate and_1 has open pins: in0=Load_A, in1=not_1_out, out=open
  // AND_Gate and_2 has open pins: in0=SELECTT, in1=Load_B, out=open
  and and_3 (and_3_out, Clock, Load_A);
  and and_4 (and_4_out, clk, Load_B);
  D_Flip_Flop d_ff_1 (.D(Data_In[3]), .clk(and_3_out), .Q(REG_A_OUT[3]));  // open: Qn, preset, reset
  D_Flip_Flop d_ff_2 (.D(DATAIN[3]), .clk(and_4_out), .Q(REG_B_OUT[3]));  // open: Qn, preset, reset
  D_Flip_Flop d_ff_3 (.D(Data_In[2]), .clk(and_3_out), .Q(REG_A_OUT[2]));  // open: Qn, preset, reset
  D_Flip_Flop d_ff_4 (.D(DATAIN[2]), .clk(and_4_out), .Q(REG_B_OUT[2]));  // open: Qn, preset, reset
  D_Flip_Flop d_ff_5 (.D(Data_In[1]), .clk(and_3_out), .Q(REG_A_OUT[1]));  // open: Qn, preset, reset
  D_Flip_Flop d_ff_6 (.D(DATAIN[1]), .clk(and_4_out), .Q(REG_B_OUT[1]));  // open: Qn, preset, reset
  D_Flip_Flop d_ff_7 (.D(Data_In[0]), .clk(and_3_out), .Q(REG_A_OUT[0]));  // open: Qn, preset, reset
  D_Flip_Flop d_ff_8 (.D(DATAIN[0]), .clk(and_4_out), .Q(REG_B_OUT[0]));  // open: Qn, preset, reset
endmodule
